# Fritzing sketch pcbPololu_1b (saved by Fritzing 0.7.12b)
breadboards: 1

parts:
  Power_plug1 = Power plug  # not connected
  Arduino1 = Arduino
  R1 = Resistor [tolerance=±5% resistance=10k package=THT]
  R2 = Resistor [tolerance=±5% resistance=10k package=THT]
  R3 = Resistor [tolerance=±5% resistance=0 package=THT]
  J8 = screw terminal, 2 pins  # not connected
  J9 = screw terminal, 2 pins  # not connected
  J10 = screw terminal, 2 pins
  J11 = screw terminal, 2 pins
  J12 = screw terminal, 2 pins  # not connected
  J14 = screw terminal, 2 pins  # not connected

nets:
  N1: Arduino1.GND, R1.Pin_0, R2.Pin_0, R3.Pin_0
  N2: Arduino1.D11, R1.Pin_1, J11.pin2
  N3: Arduino1.D10, R2.Pin_1, J10.pin2
  N4: Arduino1.+5V, J10.pin1, J11.pin1

notes:
  pololu_1b
  19/12/2013
  1
